# Fritzing sketch SmartCup (saved by Fritzing 1.0.2b)
breadboards: 1

parts:
  Load_Cell1 = Load Cell - Red/white/black/green
  Part1 = HX711 Weighing Sensor Module
  Componente5 = Arduino Mega 2560 (Rev3)
  R2 = Resistor [tolerance=±5% resistance=30 package="1206 [SMD]"]
  Componente7 = adafruit [part_number=1586]
  Componente8 = RFID-RC522

nets:
  N1: Load_Cell1.wire1, Part1.E+
  N2: Load_Cell1.wire2, Part1.A+
  N3: Load_Cell1.wire3, Part1.E-
  N4: Load_Cell1.wire4, Part1.A-
  VCC: Part1.VCC, Componente5.5V, Componente7.connector39
  GND: Part1.GND, Componente5.GND, Componente7.connector42, Componente8.connector13
  N5: Part1.DO/RX, Componente5.D3_PWM
  N6: Part1.CK/TX, Componente5.D2_PWM
  N7: Componente5.3V3, Componente8.connector15
  N8: Componente5.D4_PWM, R2.Pin_1
  N9: Componente5.D49, Componente8.connector14
  N10: Componente5.D50, Componente8.connector11
  N11: Componente5.D51, Componente8.connector10
  N12: Componente5.D52, Componente8.connector9
  N13: Componente5.D53, Componente8.connector8
  N14: R2.Pin_0, Componente7.connector37

custom parts:
  Load Cell - Red/white/black/green: A rectangle load cell/weighting pressure Sensor with four wires - Red, white, black, green. Normally corresponding with E+, E-, A+, A- respectively.
  HX711 Weighing Sensor Module: HX711 is a precision 24-bit analog-to-digital converter (ADC) designed for weigh scales and industrial control applications to interface directly with a bridge sensor.
